# Fritzing sketch brewbuild_test_platform (saved by Fritzing 0.9.3b)
breadboards: 1

parts:
  Raspberry_Pi_1 = Raspberry Pi 3 [part_number=RPI-3-V1.2]
  IC1 = MCP3008 8-channel 10-bit ADC [part_number=MCP3008]
  IC2 = IC, DIP package, 14 pins [chip_label=MCP4922]
  U1 = 74HC595 SMD [package="SO16 [SMD]"]

nets:
  3V3: Raspberry_Pi_1.3v3, IC1.no_name_yet#15, IC1.no_name_yet#16, IC2.pin1, IC2.pin8, IC2.pin9, IC2.pin12, U1.MR, U1.VCC
  N1: Raspberry_Pi_1.GIPO10, IC1.no_name_yet#11, IC2.pin5
  N2: Raspberry_Pi_1.GIPO9, IC1.no_name_yet#12
  N3: Raspberry_Pi_1.GIPO11, IC1.no_name_yet#13, IC2.pin4
  GND: Raspberry_Pi_1.GND, IC1.no_name_yet#9, IC1.no_name_yet#14, IC2.pin11, IC2.pin13, U1.GND, U1.OE
  N4: Raspberry_Pi_1.GIPO21, U1.DS
  N5: Raspberry_Pi_1.GIPO20, U1.SH_CP
  N6: Raspberry_Pi_1.GIPO16, U1.ST_CP
  N7: Raspberry_Pi_1.GIPO12, IC2.pin3
  N8: Raspberry_Pi_1.GIPO8, IC1.no_name_yet#10
  N9: IC1.no_name_yet#1, U1.Q0
  N10: IC1.no_name_yet#2, IC2.pin14
  N11: IC1.no_name_yet#3, U1.Q1

notes:
  RPi 3 Test Platform
  ----------------------------------------
  ADC (MCP3008):
  Yellow: ADC 13 <-> GPIO11 (SCLK)
  White: ADC 12 <-> GPIO9 (MISO)
  Orange: ADC 11 <-> GPIO10 (MOSI)
  Purple: ADC 10 (CS) <-> GPIO26
  DAC (MCP4922):
  Green: DAC LDAC 8 <-> Gnd
  Brown: DAC Out0 <-> ADC In1
  Lt. Blue DAC CS 3 <-> GPIO 12
  Yellow DAC SCK 4 <-> GPIO11 (SCLK)
  Orange DAC SDI 5 <-> GPIO10 (MOSI)
  Shift Register (74HC595):
  Grey0: SR Out0 <-> ADC In0
  Grey1: SR Out1 <->ADC In2
  Blue: SR DATA 14 <-> GPIO 21
  White: SR STCP (LATCH) 12 <-> GPIO 16
  Pink: SR SHCP (CLK) 11 <-> GPIO 20
