# Fritzing sketch two_74595_shift_registers (saved by Fritzing 0.9.3b)
breadboards: 3

parts:
  Raspberry_Pi_1 = Raspberry Pi 3 [part_number=RPI-3-V1.2]
  U2 = 74HC595 [package="DIP16 [THT]"]
  U1 = 74HC595 [package="DIP16 [THT]"]
  LED1 = smd LED [color="Yellow (595nm)" package="1206 [SMD]"]
  LED12 = smd LED [color="Blue (525nm)" package="1206 [SMD]"]
  LED14 = smd LED [color="Blue (525nm)" package="1206 [SMD]"]
  LED17 = smd LED [color="Blue (525nm)" package="1206 [SMD]"]
  R4 = Resistor [tolerance=±5% resistance=220 package="0402 [SMD]"]
  R5 = Resistor [tolerance=±5% resistance=220 package="0402 [SMD]"]
  R3 = Resistor [tolerance=±5% resistance=220 package="0402 [SMD]"]
  R14 = Resistor [tolerance=±5% resistance=220 package="0402 [SMD]"]
  R1 = Resistor [tolerance=±5% resistance=220 package="0402 [SMD]"]
  R10 = Resistor [tolerance=±5% resistance=220 package="0402 [SMD]"]
  R12 = Resistor [tolerance=±5% resistance=220 package="0402 [SMD]"]
  R2 = Resistor [tolerance=±5% resistance=220 package="0402 [SMD]"]
  R6 = Resistor [tolerance=±5% resistance=220 package="0402 [SMD]"]
  R13 = Resistor [tolerance=±5% resistance=220 package="0402 [SMD]"]
  LED3 = smd LED [color="Yellow (595nm)" package="1206 [SMD]"]
  R15 = Resistor [tolerance=±5% resistance=220 package="0402 [SMD]"]
  LED13 = smd LED [color="Blue (525nm)" package="1206 [SMD]"]
  R7 = Resistor [tolerance=±5% resistance=220 package="0402 [SMD]"]
  R8 = Resistor [tolerance=±5% resistance=220 package="0402 [SMD]"]
  LED5 = smd LED [color="Yellow (595nm)" package="1206 [SMD]"]
  R11 = Resistor [tolerance=±5% resistance=220 package="0402 [SMD]"]
  LED16 = smd LED [color="Blue (525nm)" package="1206 [SMD]"]
  LED10 = smd LED [color="Blue (525nm)" package="1206 [SMD]"]
  LED2 = smd LED [color="Yellow (595nm)" package="1206 [SMD]"]
  LED15 = smd LED [color="Blue (525nm)" package="1206 [SMD]"]
  LED4 = smd LED [color="Yellow (595nm)" package="1206 [SMD]"]
  R9 = Resistor [tolerance=±5% resistance=220 package="0402 [SMD]"]
  R16 = Resistor [tolerance=±5% resistance=220 package="0402 [SMD]"]
  LED8 = smd LED [color="Yellow (595nm)" package="1206 [SMD]"]
  LED7 = smd LED [color="Yellow (595nm)" package="1206 [SMD]"]
  LED6 = smd LED [color="Yellow (595nm)" package="1206 [SMD]"]
  LED18 = smd LED [color="Blue (525nm)" package="1206 [SMD]"]

nets:
  3V3: Raspberry_Pi_1.3v3, Raspberry_Pi_1.3V3, U2.MR, U2.VCC, U1.MR, U1.VCC
  N1: Raspberry_Pi_1.GPIO21, U1.DS
  N2: Raspberry_Pi_1.GPIO20, U2.SH_CP, U1.SH_CP
  N3: Raspberry_Pi_1.GPIO16, U2.ST_CP, U1.ST_CP
  GND: Raspberry_Pi_1.GND, U2.GND, U2.OE, U1.GND, U1.OE, R4.Pin_1, R5.Pin_1, R3.Pin_1, R14.Pin_1, R1.Pin_1, R10.Pin_1, R12.Pin_1, R2.Pin_1, R6.Pin_1, R13.Pin_1, R15.Pin_1, R7.Pin_1, R8.Pin_1, R11.Pin_1, R9.Pin_1, R16.Pin_1
  N4: U2.Q1, LED14.anode
  N5: U2.Q2, LED12.anode
  N6: U2.Q3, LED16.anode
  N7: U2.Q4, LED10.anode
  N8: U2.Q5, LED13.anode
  N9: U2.Q6, LED15.anode
  N10: U2.Q7, LED18.anode
  N11: U2.DS, U1.Q7'
  N12: U2.Q0, LED17.anode
  N13: U1.Q1, LED2.anode
  N14: U1.Q2, LED3.anode
  N15: U1.Q3, LED4.anode
  N16: U1.Q4, LED5.anode
  N17: U1.Q5, LED6.anode
  N18: U1.Q6, LED7.anode
  N19: U1.Q7, LED8.anode
  N20: U1.Q0, LED1.anode
  N21: LED1.cathode, R1.Pin_0
  N22: LED12.cathode, R13.Pin_0
  N23: LED14.cathode, R10.Pin_0
  N24: LED17.cathode, R9.Pin_0
  N25: R4.Pin_0, LED4.cathode
  N26: R5.Pin_0, LED5.cathode
  N27: R3.Pin_0, LED3.cathode
  N28: R14.Pin_0, LED13.cathode
  N29: R12.Pin_0, LED16.cathode
  N30: R2.Pin_0, LED2.cathode
  N31: R6.Pin_0, LED6.cathode
  N32: R15.Pin_0, LED15.cathode
  N33: R7.Pin_0, LED7.cathode
  N34: R8.Pin_0, LED8.cathode
  N35: R11.Pin_0, LED10.cathode
  N36: R16.Pin_0, LED18.cathode

notes:
  Daisy-chained 74HC595 shift registers
  -----------------------------------------------------
  grey: GPIO 21 (data) <-> SR1 14 (DS)
  blue: GPIO 20 (clock) <-> SR1+2 11 (SHCP)
  white: GPIO 16 (latch) <-> SR1+2 12 (STCP)
  yellow: SR1 9 (Q7s) <-> SR2 14 (DS)
  Resistors are all 220 Ohm.
  To add additional registers to the chain, simply connect pin 9 on the last one in the chain to pin 14 (DS) to the new addition. (Shown as the yellow wire)
